// Logisim project ALU.circ as structural Verilog: 6 circuits, main circuit ALU
module ALU (
  input  [3:0] F,
  input  [7:0] A,
  input  [7:0] B,
  input  [2:0] Shift,
  output [7:0] R,
  output [4:0] Status
);

  wire [7:0] adder_1_out, adder_2_out, and_1_out, i__n_2_ausgang, i__n_ausgang, Mult_A_B_ausgang, nand_1_out,
       not_1_out, or_1_out, subtractor_1_out, subtractor_2_out, Swap_A_ausgang;

  assign not_1_out = ~A;  // NOT_Gate not_1, 8 bits wide
  Multiplexer #(.select(4), .width(8), .enable("false")) multiplexer_1 (
    .in0(A), .in1(not_1_out), .in2(B), .in3(adder_1_out), .in4(subtractor_1_out), .in5(and_1_out),
    .in6(or_1_out), .in7(nand_1_out), .in8(adder_2_out), .in9(subtractor_2_out), .in10(Mult_A_B_ausgang),
    .in11(Swap_A_ausgang), .in12(i__n_ausgang), .in13(i__n_2_ausgang), .out(R), .sel(F));  // open: in14, in15
  Adder adder_1 (.a(8'h1), .b(A), .out(adder_1_out), .cout(Status[0]));  // open: cin
  Subtractor subtractor_1 (.a(A), .b(8'h1), .out(subtractor_1_out), .bout(Status[1]));  // open: bin
  assign and_1_out = A & B;  // AND_Gate and_1, 8 bits wide
  assign or_1_out = A | B;  // OR_Gate or_1, 8 bits wide
  assign nand_1_out = ~(A & B);  // NAND_Gate nand_1, 8 bits wide
  Adder adder_2 (.a(A), .b(B), .out(adder_2_out), .cout(Status[2]));  // open: cin
  Subtractor subtractor_2 (.a(A), .b(B), .out(subtractor_2_out), .bout(Status[3]));  // open: bin
  Multiplikation Mult_A_B (.X(A), .Y(B), .Ausgang(Mult_A_B_ausgang), .Wertebereich(Status[4]));
  swap Swap_A (.Eingang(A), .Ausgang(Swap_A_ausgang));
  N_shift_links i__n (.Eingang(A), .Shift(Shift), .Ausgang(i__n_ausgang));
  N_shift_rechts i__n_2 (.Eingang(A), .Shift(Shift), .Ausgang(i__n_2_ausgang));
endmodule

module Multiplikation (
  input  [7:0] X,
  input  [7:0] Y,
  output [7:0] Ausgang,
  output Wertebereich
);

  wire [7:0] selectadd_1_c2, selectadd_2_c2, selectadd_3_c2, selectadd_4_c2, selectadd_5_c2, selectadd_6_c2,
       selectadd_7_c2, selectadd_8_c2;

  selectadd selectadd_1 (.A({8{1'b0}}), .B(X), .En(Y[0]), .C1(Ausgang[0]), .C2(selectadd_1_c2));
  selectadd selectadd_2 (.A(selectadd_1_c2), .B(X), .En(Y[1]), .C1(Ausgang[1]), .C2(selectadd_2_c2));
  selectadd selectadd_3 (.A(selectadd_2_c2), .B(X), .En(Y[2]), .C1(Ausgang[2]), .C2(selectadd_3_c2));
  selectadd selectadd_4 (.A(selectadd_3_c2), .B(X), .En(Y[3]), .C1(Ausgang[3]), .C2(selectadd_4_c2));
  selectadd selectadd_5 (.A(selectadd_4_c2), .B(X), .En(Y[4]), .C1(Ausgang[4]), .C2(selectadd_5_c2));
  selectadd selectadd_6 (.A(selectadd_5_c2), .B(X), .En(Y[5]), .C1(Ausgang[5]), .C2(selectadd_6_c2));
  selectadd selectadd_7 (.A(selectadd_6_c2), .B(X), .En(Y[6]), .C1(Ausgang[6]), .C2(selectadd_7_c2));
  selectadd selectadd_8 (.A(selectadd_7_c2), .B(X), .En(Y[7]), .C1(Ausgang[7]), .C2(selectadd_8_c2));
  or or_1 (Wertebereich, selectadd_8_c2[0], selectadd_8_c2[1], selectadd_8_c2[2], selectadd_8_c2[3], selectadd_8_c2[4], selectadd_8_c2[5], selectadd_8_c2[6], selectadd_8_c2[7]);
endmodule

module swap (
  input  [7:0] Eingang,
  output [7:0] Ausgang
);


  assign Ausgang = {Eingang[3:0], Eingang[7:4]};
endmodule

module N_shift_links (
  input  [7:0] Eingang,
  input  [2:0] Shift,
  output [7:0] Ausgang
);

  wire decoder_1_out0, decoder_1_out1, decoder_1_out2, decoder_1_out3, decoder_1_out4, decoder_1_out5,
       decoder_1_out6, decoder_1_out7;

  Decoder #(.select(3), .enable("false")) decoder_1 (
    .out0(decoder_1_out0), .out1(decoder_1_out1), .out2(decoder_1_out2), .out3(decoder_1_out3),
    .out4(decoder_1_out4), .out5(decoder_1_out5), .out6(decoder_1_out6), .out7(decoder_1_out7), .sel(Shift));
  assign Ausgang[7] = decoder_1_out7 ? Eingang[0] : 1'bz;  // Controlled_Buffer controlled_buffer_1
  assign Ausgang[6] = decoder_1_out6 ? Eingang[0] : 1'bz;  // Controlled_Buffer controlled_buffer_2
  assign Ausgang[5] = decoder_1_out5 ? Eingang[0] : 1'bz;  // Controlled_Buffer controlled_buffer_3
  assign Ausgang[4] = decoder_1_out4 ? Eingang[0] : 1'bz;  // Controlled_Buffer controlled_buffer_4
  assign Ausgang[3] = decoder_1_out3 ? Eingang[0] : 1'bz;  // Controlled_Buffer controlled_buffer_5
  assign Ausgang[2] = decoder_1_out2 ? Eingang[0] : 1'bz;  // Controlled_Buffer controlled_buffer_6
  assign Ausgang[1] = decoder_1_out1 ? Eingang[0] : 1'bz;  // Controlled_Buffer controlled_buffer_7
  assign Ausgang[0] = decoder_1_out0 ? Eingang[0] : 1'bz;  // Controlled_Buffer controlled_buffer_8
  assign Ausgang[7] = decoder_1_out6 ? Eingang[1] : 1'bz;  // Controlled_Buffer controlled_buffer_9
  assign Ausgang[6] = decoder_1_out5 ? Eingang[1] : 1'bz;  // Controlled_Buffer controlled_buffer_10
  assign Ausgang[5] = decoder_1_out4 ? Eingang[1] : 1'bz;  // Controlled_Buffer controlled_buffer_11
  assign Ausgang[4] = decoder_1_out3 ? Eingang[1] : 1'bz;  // Controlled_Buffer controlled_buffer_12
  assign Ausgang[3] = decoder_1_out2 ? Eingang[1] : 1'bz;  // Controlled_Buffer controlled_buffer_13
  assign Ausgang[2] = decoder_1_out1 ? Eingang[1] : 1'bz;  // Controlled_Buffer controlled_buffer_14
  assign Ausgang[1] = decoder_1_out0 ? Eingang[1] : 1'bz;  // Controlled_Buffer controlled_buffer_15
  assign Ausgang[0] = decoder_1_out7 ? Eingang[1] : 1'bz;  // Controlled_Buffer controlled_buffer_16
  assign Ausgang[7] = decoder_1_out5 ? Eingang[2] : 1'bz;  // Controlled_Buffer controlled_buffer_17
  assign Ausgang[6] = decoder_1_out4 ? Eingang[2] : 1'bz;  // Controlled_Buffer controlled_buffer_18
  assign Ausgang[5] = decoder_1_out3 ? Eingang[2] : 1'bz;  // Controlled_Buffer controlled_buffer_19
  assign Ausgang[4] = decoder_1_out2 ? Eingang[2] : 1'bz;  // Controlled_Buffer controlled_buffer_20
  assign Ausgang[3] = decoder_1_out1 ? Eingang[2] : 1'bz;  // Controlled_Buffer controlled_buffer_21
  assign Ausgang[2] = decoder_1_out0 ? Eingang[2] : 1'bz;  // Controlled_Buffer controlled_buffer_22
  assign Ausgang[1] = decoder_1_out7 ? Eingang[2] : 1'bz;  // Controlled_Buffer controlled_buffer_23
  assign Ausgang[0] = decoder_1_out6 ? Eingang[2] : 1'bz;  // Controlled_Buffer controlled_buffer_24
  assign Ausgang[7] = decoder_1_out4 ? Eingang[3] : 1'bz;  // Controlled_Buffer controlled_buffer_25
  assign Ausgang[6] = decoder_1_out3 ? Eingang[3] : 1'bz;  // Controlled_Buffer controlled_buffer_26
  assign Ausgang[5] = decoder_1_out2 ? Eingang[3] : 1'bz;  // Controlled_Buffer controlled_buffer_27
  assign Ausgang[4] = decoder_1_out1 ? Eingang[3] : 1'bz;  // Controlled_Buffer controlled_buffer_28
  assign Ausgang[3] = decoder_1_out0 ? Eingang[3] : 1'bz;  // Controlled_Buffer controlled_buffer_29
  assign Ausgang[2] = decoder_1_out7 ? Eingang[3] : 1'bz;  // Controlled_Buffer controlled_buffer_30
  assign Ausgang[1] = decoder_1_out6 ? Eingang[3] : 1'bz;  // Controlled_Buffer controlled_buffer_31
  assign Ausgang[0] = decoder_1_out5 ? Eingang[3] : 1'bz;  // Controlled_Buffer controlled_buffer_32
  assign Ausgang[7] = decoder_1_out3 ? Eingang[4] : 1'bz;  // Controlled_Buffer controlled_buffer_33
  assign Ausgang[6] = decoder_1_out2 ? Eingang[4] : 1'bz;  // Controlled_Buffer controlled_buffer_34
  assign Ausgang[5] = decoder_1_out1 ? Eingang[4] : 1'bz;  // Controlled_Buffer controlled_buffer_35
  assign Ausgang[4] = decoder_1_out0 ? Eingang[4] : 1'bz;  // Controlled_Buffer controlled_buffer_36
  assign Ausgang[3] = decoder_1_out7 ? Eingang[4] : 1'bz;  // Controlled_Buffer controlled_buffer_37
  assign Ausgang[2] = decoder_1_out6 ? Eingang[4] : 1'bz;  // Controlled_Buffer controlled_buffer_38
  assign Ausgang[1] = decoder_1_out5 ? Eingang[4] : 1'bz;  // Controlled_Buffer controlled_buffer_39
  assign Ausgang[0] = decoder_1_out4 ? Eingang[4] : 1'bz;  // Controlled_Buffer controlled_buffer_40
  assign Ausgang[7] = decoder_1_out2 ? Eingang[5] : 1'bz;  // Controlled_Buffer controlled_buffer_41
  assign Ausgang[6] = decoder_1_out1 ? Eingang[5] : 1'bz;  // Controlled_Buffer controlled_buffer_42
  assign Ausgang[5] = decoder_1_out0 ? Eingang[5] : 1'bz;  // Controlled_Buffer controlled_buffer_43
  assign Ausgang[4] = decoder_1_out7 ? Eingang[5] : 1'bz;  // Controlled_Buffer controlled_buffer_44
  assign Ausgang[3] = decoder_1_out6 ? Eingang[5] : 1'bz;  // Controlled_Buffer controlled_buffer_45
  assign Ausgang[2] = decoder_1_out5 ? Eingang[5] : 1'bz;  // Controlled_Buffer controlled_buffer_46
  assign Ausgang[1] = decoder_1_out4 ? Eingang[5] : 1'bz;  // Controlled_Buffer controlled_buffer_47
  assign Ausgang[0] = decoder_1_out3 ? Eingang[5] : 1'bz;  // Controlled_Buffer controlled_buffer_48
  assign Ausgang[7] = decoder_1_out1 ? Eingang[6] : 1'bz;  // Controlled_Buffer controlled_buffer_49
  assign Ausgang[6] = decoder_1_out0 ? Eingang[6] : 1'bz;  // Controlled_Buffer controlled_buffer_50
  assign Ausgang[5] = decoder_1_out7 ? Eingang[6] : 1'bz;  // Controlled_Buffer controlled_buffer_51
  assign Ausgang[4] = decoder_1_out6 ? Eingang[6] : 1'bz;  // Controlled_Buffer controlled_buffer_52
  assign Ausgang[3] = decoder_1_out5 ? Eingang[6] : 1'bz;  // Controlled_Buffer controlled_buffer_53
  assign Ausgang[2] = decoder_1_out4 ? Eingang[6] : 1'bz;  // Controlled_Buffer controlled_buffer_54
  assign Ausgang[1] = decoder_1_out3 ? Eingang[6] : 1'bz;  // Controlled_Buffer controlled_buffer_55
  assign Ausgang[0] = decoder_1_out2 ? Eingang[6] : 1'bz;  // Controlled_Buffer controlled_buffer_56
  assign Ausgang[7] = decoder_1_out0 ? Eingang[7] : 1'bz;  // Controlled_Buffer controlled_buffer_57
  assign Ausgang[6] = decoder_1_out7 ? Eingang[7] : 1'bz;  // Controlled_Buffer controlled_buffer_58
  assign Ausgang[5] = decoder_1_out6 ? Eingang[7] : 1'bz;  // Controlled_Buffer controlled_buffer_59
  assign Ausgang[4] = decoder_1_out5 ? Eingang[7] : 1'bz;  // Controlled_Buffer controlled_buffer_60
  assign Ausgang[3] = decoder_1_out4 ? Eingang[7] : 1'bz;  // Controlled_Buffer controlled_buffer_61
  assign Ausgang[2] = decoder_1_out3 ? Eingang[7] : 1'bz;  // Controlled_Buffer controlled_buffer_62
  assign Ausgang[1] = decoder_1_out2 ? Eingang[7] : 1'bz;  // Controlled_Buffer controlled_buffer_63
  assign Ausgang[0] = decoder_1_out1 ? Eingang[7] : 1'bz;  // Controlled_Buffer controlled_buffer_64
endmodule

module N_shift_rechts (
  input  [7:0] Eingang,
  input  [2:0] Shift,
  output [7:0] Ausgang
);

  wire decoder_1_out0, decoder_1_out1, decoder_1_out2, decoder_1_out3, decoder_1_out4, decoder_1_out5,
       decoder_1_out6, decoder_1_out7;

  Decoder #(.select(3), .enable("false")) decoder_1 (
    .out0(decoder_1_out0), .out1(decoder_1_out1), .out2(decoder_1_out2), .out3(decoder_1_out3),
    .out4(decoder_1_out4), .out5(decoder_1_out5), .out6(decoder_1_out6), .out7(decoder_1_out7), .sel(Shift));
  assign Ausgang[7] = decoder_1_out1 ? Eingang[0] : 1'bz;  // Controlled_Buffer controlled_buffer_1
  assign Ausgang[6] = decoder_1_out2 ? Eingang[0] : 1'bz;  // Controlled_Buffer controlled_buffer_2
  assign Ausgang[5] = decoder_1_out3 ? Eingang[0] : 1'bz;  // Controlled_Buffer controlled_buffer_3
  assign Ausgang[4] = decoder_1_out4 ? Eingang[0] : 1'bz;  // Controlled_Buffer controlled_buffer_4
  assign Ausgang[3] = decoder_1_out5 ? Eingang[0] : 1'bz;  // Controlled_Buffer controlled_buffer_5
  assign Ausgang[2] = decoder_1_out6 ? Eingang[0] : 1'bz;  // Controlled_Buffer controlled_buffer_6
  assign Ausgang[1] = decoder_1_out7 ? Eingang[0] : 1'bz;  // Controlled_Buffer controlled_buffer_7
  assign Ausgang[0] = decoder_1_out0 ? Eingang[0] : 1'bz;  // Controlled_Buffer controlled_buffer_8
  assign Ausgang[7] = decoder_1_out2 ? Eingang[1] : 1'bz;  // Controlled_Buffer controlled_buffer_9
  assign Ausgang[6] = decoder_1_out3 ? Eingang[1] : 1'bz;  // Controlled_Buffer controlled_buffer_10
  assign Ausgang[5] = decoder_1_out4 ? Eingang[1] : 1'bz;  // Controlled_Buffer controlled_buffer_11
  assign Ausgang[4] = decoder_1_out5 ? Eingang[1] : 1'bz;  // Controlled_Buffer controlled_buffer_12
  assign Ausgang[3] = decoder_1_out6 ? Eingang[1] : 1'bz;  // Controlled_Buffer controlled_buffer_13
  assign Ausgang[2] = decoder_1_out7 ? Eingang[1] : 1'bz;  // Controlled_Buffer controlled_buffer_14
  assign Ausgang[1] = decoder_1_out0 ? Eingang[1] : 1'bz;  // Controlled_Buffer controlled_buffer_15
  assign Ausgang[0] = decoder_1_out1 ? Eingang[1] : 1'bz;  // Controlled_Buffer controlled_buffer_16
  assign Ausgang[7] = decoder_1_out3 ? Eingang[2] : 1'bz;  // Controlled_Buffer controlled_buffer_17
  assign Ausgang[6] = decoder_1_out4 ? Eingang[2] : 1'bz;  // Controlled_Buffer controlled_buffer_18
  assign Ausgang[5] = decoder_1_out5 ? Eingang[2] : 1'bz;  // Controlled_Buffer controlled_buffer_19
  assign Ausgang[4] = decoder_1_out6 ? Eingang[2] : 1'bz;  // Controlled_Buffer controlled_buffer_20
  assign Ausgang[3] = decoder_1_out7 ? Eingang[2] : 1'bz;  // Controlled_Buffer controlled_buffer_21
  assign Ausgang[2] = decoder_1_out0 ? Eingang[2] : 1'bz;  // Controlled_Buffer controlled_buffer_22
  assign Ausgang[1] = decoder_1_out1 ? Eingang[2] : 1'bz;  // Controlled_Buffer controlled_buffer_23
  assign Ausgang[0] = decoder_1_out2 ? Eingang[2] : 1'bz;  // Controlled_Buffer controlled_buffer_24
  assign Ausgang[7] = decoder_1_out4 ? Eingang[3] : 1'bz;  // Controlled_Buffer controlled_buffer_25
  assign Ausgang[6] = decoder_1_out5 ? Eingang[3] : 1'bz;  // Controlled_Buffer controlled_buffer_26
  assign Ausgang[5] = decoder_1_out6 ? Eingang[3] : 1'bz;  // Controlled_Buffer controlled_buffer_27
  assign Ausgang[4] = decoder_1_out7 ? Eingang[3] : 1'bz;  // Controlled_Buffer controlled_buffer_28
  assign Ausgang[3] = decoder_1_out0 ? Eingang[3] : 1'bz;  // Controlled_Buffer controlled_buffer_29
  assign Ausgang[2] = decoder_1_out1 ? Eingang[3] : 1'bz;  // Controlled_Buffer controlled_buffer_30
  assign Ausgang[1] = decoder_1_out2 ? Eingang[3] : 1'bz;  // Controlled_Buffer controlled_buffer_31
  assign Ausgang[0] = decoder_1_out3 ? Eingang[3] : 1'bz;  // Controlled_Buffer controlled_buffer_32
  assign Ausgang[7] = decoder_1_out5 ? Eingang[4] : 1'bz;  // Controlled_Buffer controlled_buffer_33
  assign Ausgang[6] = decoder_1_out6 ? Eingang[4] : 1'bz;  // Controlled_Buffer controlled_buffer_34
  assign Ausgang[5] = decoder_1_out7 ? Eingang[4] : 1'bz;  // Controlled_Buffer controlled_buffer_35
  assign Ausgang[4] = decoder_1_out0 ? Eingang[4] : 1'bz;  // Controlled_Buffer controlled_buffer_36
  assign Ausgang[3] = decoder_1_out1 ? Eingang[4] : 1'bz;  // Controlled_Buffer controlled_buffer_37
  assign Ausgang[2] = decoder_1_out2 ? Eingang[4] : 1'bz;  // Controlled_Buffer controlled_buffer_38
  assign Ausgang[1] = decoder_1_out3 ? Eingang[4] : 1'bz;  // Controlled_Buffer controlled_buffer_39
  assign Ausgang[0] = decoder_1_out4 ? Eingang[4] : 1'bz;  // Controlled_Buffer controlled_buffer_40
  assign Ausgang[7] = decoder_1_out6 ? Eingang[5] : 1'bz;  // Controlled_Buffer controlled_buffer_41
  assign Ausgang[6] = decoder_1_out7 ? Eingang[5] : 1'bz;  // Controlled_Buffer controlled_buffer_42
  assign Ausgang[5] = decoder_1_out0 ? Eingang[5] : 1'bz;  // Controlled_Buffer controlled_buffer_43
  assign Ausgang[4] = decoder_1_out1 ? Eingang[5] : 1'bz;  // Controlled_Buffer controlled_buffer_44
  assign Ausgang[3] = decoder_1_out2 ? Eingang[5] : 1'bz;  // Controlled_Buffer controlled_buffer_45
  assign Ausgang[2] = decoder_1_out3 ? Eingang[5] : 1'bz;  // Controlled_Buffer controlled_buffer_46
  assign Ausgang[1] = decoder_1_out4 ? Eingang[5] : 1'bz;  // Controlled_Buffer controlled_buffer_47
  assign Ausgang[0] = decoder_1_out5 ? Eingang[5] : 1'bz;  // Controlled_Buffer controlled_buffer_48
  assign Ausgang[7] = decoder_1_out7 ? Eingang[6] : 1'bz;  // Controlled_Buffer controlled_buffer_49
  assign Ausgang[6] = decoder_1_out0 ? Eingang[6] : 1'bz;  // Controlled_Buffer controlled_buffer_50
  assign Ausgang[5] = decoder_1_out1 ? Eingang[6] : 1'bz;  // Controlled_Buffer controlled_buffer_51
  assign Ausgang[4] = decoder_1_out2 ? Eingang[6] : 1'bz;  // Controlled_Buffer controlled_buffer_52
  assign Ausgang[3] = decoder_1_out3 ? Eingang[6] : 1'bz;  // Controlled_Buffer controlled_buffer_53
  assign Ausgang[2] = decoder_1_out4 ? Eingang[6] : 1'bz;  // Controlled_Buffer controlled_buffer_54
  assign Ausgang[1] = decoder_1_out5 ? Eingang[6] : 1'bz;  // Controlled_Buffer controlled_buffer_55
  assign Ausgang[0] = decoder_1_out6 ? Eingang[6] : 1'bz;  // Controlled_Buffer controlled_buffer_56
  assign Ausgang[7] = decoder_1_out0 ? Eingang[7] : 1'bz;  // Controlled_Buffer controlled_buffer_57
  assign Ausgang[6] = decoder_1_out1 ? Eingang[7] : 1'bz;  // Controlled_Buffer controlled_buffer_58
  assign Ausgang[5] = decoder_1_out2 ? Eingang[7] : 1'bz;  // Controlled_Buffer controlled_buffer_59
  assign Ausgang[4] = decoder_1_out3 ? Eingang[7] : 1'bz;  // Controlled_Buffer controlled_buffer_60
  assign Ausgang[3] = decoder_1_out4 ? Eingang[7] : 1'bz;  // Controlled_Buffer controlled_buffer_61
  assign Ausgang[2] = decoder_1_out5 ? Eingang[7] : 1'bz;  // Controlled_Buffer controlled_buffer_62
  assign Ausgang[1] = decoder_1_out6 ? Eingang[7] : 1'bz;  // Controlled_Buffer controlled_buffer_63
  assign Ausgang[0] = decoder_1_out7 ? Eingang[7] : 1'bz;  // Controlled_Buffer controlled_buffer_64
endmodule

module selectadd (
  input  [7:0] A,
  input  [7:0] B,
  input  En,
  output C1,
  output [7:0] C2
);

  wire not_1_out;
  wire [7:0] multiplexer_1_out;

  not not_1 (not_1_out, En);
  Multiplexer #(.width(8), .enable("false")) multiplexer_1 (
    .in0(B), .in1({8{1'b0}}), .out(multiplexer_1_out), .sel(not_1_out));
  Adder adder_1 (.a(A), .b(multiplexer_1_out), .out({C2[6:0], C1}), .cout(C2[7]));  // open: cin
endmodule
