// Logisim project CPU.circ as structural Verilog: 9 circuits, main circuit main
module ALU (
  input  [3:0] F,
  input  [7:0] A,
  input  [7:0] B,
  output [7:0] R,
  output [5:0] Status
);

  wire [7:0] adder_1_out, adder_2_out, and_1_out, i__n_2_ausgang, i__n_ausgang, Mult_A_B_ausgang, nand_1_out,
       not_1_out, or_1_out, subtractor_1_out, subtractor_2_out, Swap_A_ausgang;

  assign not_1_out = ~A;  // NOT_Gate not_1, 8 bits wide
  Multiplexer #(.select(4), .width(8), .enable("false")) multiplexer_1 (
    .in0(A), .in1(not_1_out), .in2(B), .in3(adder_1_out), .in4(subtractor_1_out), .in5(and_1_out),
    .in6(or_1_out), .in7(nand_1_out), .in8(adder_2_out), .in9(subtractor_2_out), .in10(Mult_A_B_ausgang),
    .in11(Swap_A_ausgang), .in12(i__n_ausgang), .in13(i__n_2_ausgang), .out(R), .sel(F));  // open: in14, in15
  Adder adder_1 (.a(8'h1), .b(A), .out(adder_1_out), .cout(Status[0]));  // open: cin
  Subtractor subtractor_1 (.a(A), .b(8'h1), .out(subtractor_1_out), .bout(Status[1]));  // open: bin
  assign and_1_out = A & B;  // AND_Gate and_1, 8 bits wide
  assign or_1_out = A | B;  // OR_Gate or_1, 8 bits wide
  assign nand_1_out = ~(A & B);  // NAND_Gate nand_1, 8 bits wide
  Adder adder_2 (.a(A), .b(B), .out(adder_2_out), .cout(Status[2]));  // open: cin
  Subtractor subtractor_2 (.a(A), .b(B), .out(subtractor_2_out), .bout(Status[3]));  // open: bin
  Multiplikation Mult_A_B (.X(A), .Y(B), .Ausgang(Mult_A_B_ausgang), .Wertebereich(Status[4]));
  swap Swap_A (.Eingang(A), .Ausgang(Swap_A_ausgang));
  N_shift_links i__n (.Eingang(A), .Shift(3'b001), .Ausgang(i__n_ausgang));
  N_shift_rechts i__n_2 (.Eingang(A), .Shift(3'b001), .Ausgang(i__n_2_ausgang));
  nor nor_1 (Status[5], subtractor_2_out[0], subtractor_2_out[1], subtractor_2_out[2], subtractor_2_out[3], subtractor_2_out[4], subtractor_2_out[5], subtractor_2_out[6], subtractor_2_out[7]);
endmodule

module Multiplikation (
  input  [7:0] X,
  input  [7:0] Y,
  output [7:0] Ausgang,
  output Wertebereich
);

  wire [7:0] selectadd_1_c2, selectadd_2_c2, selectadd_3_c2, selectadd_4_c2, selectadd_5_c2, selectadd_6_c2,
       selectadd_7_c2, selectadd_8_c2;

  selectadd selectadd_1 (.A({8{1'b0}}), .B(X), .En(Y[0]), .C1(Ausgang[0]), .C2(selectadd_1_c2));
  selectadd selectadd_2 (.A(selectadd_1_c2), .B(X), .En(Y[1]), .C1(Ausgang[1]), .C2(selectadd_2_c2));
  selectadd selectadd_3 (.A(selectadd_2_c2), .B(X), .En(Y[2]), .C1(Ausgang[2]), .C2(selectadd_3_c2));
  selectadd selectadd_4 (.A(selectadd_3_c2), .B(X), .En(Y[3]), .C1(Ausgang[3]), .C2(selectadd_4_c2));
  selectadd selectadd_5 (.A(selectadd_4_c2), .B(X), .En(Y[4]), .C1(Ausgang[4]), .C2(selectadd_5_c2));
  selectadd selectadd_6 (.A(selectadd_5_c2), .B(X), .En(Y[5]), .C1(Ausgang[5]), .C2(selectadd_6_c2));
  selectadd selectadd_7 (.A(selectadd_6_c2), .B(X), .En(Y[6]), .C1(Ausgang[6]), .C2(selectadd_7_c2));
  selectadd selectadd_8 (.A(selectadd_7_c2), .B(X), .En(Y[7]), .C1(Ausgang[7]), .C2(selectadd_8_c2));
  or or_1 (Wertebereich, selectadd_8_c2[0], selectadd_8_c2[1], selectadd_8_c2[2], selectadd_8_c2[3], selectadd_8_c2[4], selectadd_8_c2[5], selectadd_8_c2[6], selectadd_8_c2[7]);
endmodule

module swap (
  input  [7:0] Eingang,
  output [7:0] Ausgang
);


  assign Ausgang = {Eingang[3:0], Eingang[7:4]};
endmodule

module N_shift_links (
  input  [7:0] Eingang,
  input  [2:0] Shift,
  output [7:0] Ausgang
);

  wire decoder_1_out0, decoder_1_out1, decoder_1_out2, decoder_1_out3, decoder_1_out4, decoder_1_out5,
       decoder_1_out6, decoder_1_out7;

  Decoder #(.select(3), .enable("false")) decoder_1 (
    .out0(decoder_1_out0), .out1(decoder_1_out1), .out2(decoder_1_out2), .out3(decoder_1_out3),
    .out4(decoder_1_out4), .out5(decoder_1_out5), .out6(decoder_1_out6), .out7(decoder_1_out7), .sel(Shift));
  assign Ausgang[7] = decoder_1_out7 ? Eingang[0] : 1'bz;  // Controlled_Buffer controlled_buffer_1
  assign Ausgang[6] = decoder_1_out6 ? Eingang[0] : 1'bz;  // Controlled_Buffer controlled_buffer_2
  assign Ausgang[5] = decoder_1_out5 ? Eingang[0] : 1'bz;  // Controlled_Buffer controlled_buffer_3
  assign Ausgang[4] = decoder_1_out4 ? Eingang[0] : 1'bz;  // Controlled_Buffer controlled_buffer_4
  assign Ausgang[3] = decoder_1_out3 ? Eingang[0] : 1'bz;  // Controlled_Buffer controlled_buffer_5
  assign Ausgang[2] = decoder_1_out2 ? Eingang[0] : 1'bz;  // Controlled_Buffer controlled_buffer_6
  assign Ausgang[1] = decoder_1_out1 ? Eingang[0] : 1'bz;  // Controlled_Buffer controlled_buffer_7
  assign Ausgang[0] = decoder_1_out0 ? Eingang[0] : 1'bz;  // Controlled_Buffer controlled_buffer_8
  assign Ausgang[7] = decoder_1_out6 ? Eingang[1] : 1'bz;  // Controlled_Buffer controlled_buffer_9
  assign Ausgang[6] = decoder_1_out5 ? Eingang[1] : 1'bz;  // Controlled_Buffer controlled_buffer_10
  assign Ausgang[5] = decoder_1_out4 ? Eingang[1] : 1'bz;  // Controlled_Buffer controlled_buffer_11
  assign Ausgang[4] = decoder_1_out3 ? Eingang[1] : 1'bz;  // Controlled_Buffer controlled_buffer_12
  assign Ausgang[3] = decoder_1_out2 ? Eingang[1] : 1'bz;  // Controlled_Buffer controlled_buffer_13
  assign Ausgang[2] = decoder_1_out1 ? Eingang[1] : 1'bz;  // Controlled_Buffer controlled_buffer_14
  assign Ausgang[1] = decoder_1_out0 ? Eingang[1] : 1'bz;  // Controlled_Buffer controlled_buffer_15
  assign Ausgang[0] = decoder_1_out7 ? Eingang[1] : 1'bz;  // Controlled_Buffer controlled_buffer_16
  assign Ausgang[7] = decoder_1_out5 ? Eingang[2] : 1'bz;  // Controlled_Buffer controlled_buffer_17
  assign Ausgang[6] = decoder_1_out4 ? Eingang[2] : 1'bz;  // Controlled_Buffer controlled_buffer_18
  assign Ausgang[5] = decoder_1_out3 ? Eingang[2] : 1'bz;  // Controlled_Buffer controlled_buffer_19
  assign Ausgang[4] = decoder_1_out2 ? Eingang[2] : 1'bz;  // Controlled_Buffer controlled_buffer_20
  assign Ausgang[3] = decoder_1_out1 ? Eingang[2] : 1'bz;  // Controlled_Buffer controlled_buffer_21
  assign Ausgang[2] = decoder_1_out0 ? Eingang[2] : 1'bz;  // Controlled_Buffer controlled_buffer_22
  assign Ausgang[1] = decoder_1_out7 ? Eingang[2] : 1'bz;  // Controlled_Buffer controlled_buffer_23
  assign Ausgang[0] = decoder_1_out6 ? Eingang[2] : 1'bz;  // Controlled_Buffer controlled_buffer_24
  assign Ausgang[7] = decoder_1_out4 ? Eingang[3] : 1'bz;  // Controlled_Buffer controlled_buffer_25
  assign Ausgang[6] = decoder_1_out3 ? Eingang[3] : 1'bz;  // Controlled_Buffer controlled_buffer_26
  assign Ausgang[5] = decoder_1_out2 ? Eingang[3] : 1'bz;  // Controlled_Buffer controlled_buffer_27
  assign Ausgang[4] = decoder_1_out1 ? Eingang[3] : 1'bz;  // Controlled_Buffer controlled_buffer_28
  assign Ausgang[3] = decoder_1_out0 ? Eingang[3] : 1'bz;  // Controlled_Buffer controlled_buffer_29
  assign Ausgang[2] = decoder_1_out7 ? Eingang[3] : 1'bz;  // Controlled_Buffer controlled_buffer_30
  assign Ausgang[1] = decoder_1_out6 ? Eingang[3] : 1'bz;  // Controlled_Buffer controlled_buffer_31
  assign Ausgang[0] = decoder_1_out5 ? Eingang[3] : 1'bz;  // Controlled_Buffer controlled_buffer_32
  assign Ausgang[7] = decoder_1_out3 ? Eingang[4] : 1'bz;  // Controlled_Buffer controlled_buffer_33
  assign Ausgang[6] = decoder_1_out2 ? Eingang[4] : 1'bz;  // Controlled_Buffer controlled_buffer_34
  assign Ausgang[5] = decoder_1_out1 ? Eingang[4] : 1'bz;  // Controlled_Buffer controlled_buffer_35
  assign Ausgang[4] = decoder_1_out0 ? Eingang[4] : 1'bz;  // Controlled_Buffer controlled_buffer_36
  assign Ausgang[3] = decoder_1_out7 ? Eingang[4] : 1'bz;  // Controlled_Buffer controlled_buffer_37
  assign Ausgang[2] = decoder_1_out6 ? Eingang[4] : 1'bz;  // Controlled_Buffer controlled_buffer_38
  assign Ausgang[1] = decoder_1_out5 ? Eingang[4] : 1'bz;  // Controlled_Buffer controlled_buffer_39
  assign Ausgang[0] = decoder_1_out4 ? Eingang[4] : 1'bz;  // Controlled_Buffer controlled_buffer_40
  assign Ausgang[7] = decoder_1_out2 ? Eingang[5] : 1'bz;  // Controlled_Buffer controlled_buffer_41
  assign Ausgang[6] = decoder_1_out1 ? Eingang[5] : 1'bz;  // Controlled_Buffer controlled_buffer_42
  assign Ausgang[5] = decoder_1_out0 ? Eingang[5] : 1'bz;  // Controlled_Buffer controlled_buffer_43
  assign Ausgang[4] = decoder_1_out7 ? Eingang[5] : 1'bz;  // Controlled_Buffer controlled_buffer_44
  assign Ausgang[3] = decoder_1_out6 ? Eingang[5] : 1'bz;  // Controlled_Buffer controlled_buffer_45
  assign Ausgang[2] = decoder_1_out5 ? Eingang[5] : 1'bz;  // Controlled_Buffer controlled_buffer_46
  assign Ausgang[1] = decoder_1_out4 ? Eingang[5] : 1'bz;  // Controlled_Buffer controlled_buffer_47
  assign Ausgang[0] = decoder_1_out3 ? Eingang[5] : 1'bz;  // Controlled_Buffer controlled_buffer_48
  assign Ausgang[7] = decoder_1_out1 ? Eingang[6] : 1'bz;  // Controlled_Buffer controlled_buffer_49
  assign Ausgang[6] = decoder_1_out0 ? Eingang[6] : 1'bz;  // Controlled_Buffer controlled_buffer_50
  assign Ausgang[5] = decoder_1_out7 ? Eingang[6] : 1'bz;  // Controlled_Buffer controlled_buffer_51
  assign Ausgang[4] = decoder_1_out6 ? Eingang[6] : 1'bz;  // Controlled_Buffer controlled_buffer_52
  assign Ausgang[3] = decoder_1_out5 ? Eingang[6] : 1'bz;  // Controlled_Buffer controlled_buffer_53
  assign Ausgang[2] = decoder_1_out4 ? Eingang[6] : 1'bz;  // Controlled_Buffer controlled_buffer_54
  assign Ausgang[1] = decoder_1_out3 ? Eingang[6] : 1'bz;  // Controlled_Buffer controlled_buffer_55
  assign Ausgang[0] = decoder_1_out2 ? Eingang[6] : 1'bz;  // Controlled_Buffer controlled_buffer_56
  assign Ausgang[7] = decoder_1_out0 ? Eingang[7] : 1'bz;  // Controlled_Buffer controlled_buffer_57
  assign Ausgang[6] = decoder_1_out7 ? Eingang[7] : 1'bz;  // Controlled_Buffer controlled_buffer_58
  assign Ausgang[5] = decoder_1_out6 ? Eingang[7] : 1'bz;  // Controlled_Buffer controlled_buffer_59
  assign Ausgang[4] = decoder_1_out5 ? Eingang[7] : 1'bz;  // Controlled_Buffer controlled_buffer_60
  assign Ausgang[3] = decoder_1_out4 ? Eingang[7] : 1'bz;  // Controlled_Buffer controlled_buffer_61
  assign Ausgang[2] = decoder_1_out3 ? Eingang[7] : 1'bz;  // Controlled_Buffer controlled_buffer_62
  assign Ausgang[1] = decoder_1_out2 ? Eingang[7] : 1'bz;  // Controlled_Buffer controlled_buffer_63
  assign Ausgang[0] = decoder_1_out1 ? Eingang[7] : 1'bz;  // Controlled_Buffer controlled_buffer_64
endmodule

module N_shift_rechts (
  input  [7:0] Eingang,
  input  [2:0] Shift,
  output [7:0] Ausgang
);

  wire decoder_1_out0, decoder_1_out1, decoder_1_out2, decoder_1_out3, decoder_1_out4, decoder_1_out5,
       decoder_1_out6, decoder_1_out7;

  Decoder #(.select(3), .enable("false")) decoder_1 (
    .out0(decoder_1_out0), .out1(decoder_1_out1), .out2(decoder_1_out2), .out3(decoder_1_out3),
    .out4(decoder_1_out4), .out5(decoder_1_out5), .out6(decoder_1_out6), .out7(decoder_1_out7), .sel(Shift));
  assign Ausgang[7] = decoder_1_out1 ? Eingang[0] : 1'bz;  // Controlled_Buffer controlled_buffer_1
  assign Ausgang[6] = decoder_1_out2 ? Eingang[0] : 1'bz;  // Controlled_Buffer controlled_buffer_2
  assign Ausgang[5] = decoder_1_out3 ? Eingang[0] : 1'bz;  // Controlled_Buffer controlled_buffer_3
  assign Ausgang[4] = decoder_1_out4 ? Eingang[0] : 1'bz;  // Controlled_Buffer controlled_buffer_4
  assign Ausgang[3] = decoder_1_out5 ? Eingang[0] : 1'bz;  // Controlled_Buffer controlled_buffer_5
  assign Ausgang[2] = decoder_1_out6 ? Eingang[0] : 1'bz;  // Controlled_Buffer controlled_buffer_6
  assign Ausgang[1] = decoder_1_out7 ? Eingang[0] : 1'bz;  // Controlled_Buffer controlled_buffer_7
  assign Ausgang[0] = decoder_1_out0 ? Eingang[0] : 1'bz;  // Controlled_Buffer controlled_buffer_8
  assign Ausgang[7] = decoder_1_out2 ? Eingang[1] : 1'bz;  // Controlled_Buffer controlled_buffer_9
  assign Ausgang[6] = decoder_1_out3 ? Eingang[1] : 1'bz;  // Controlled_Buffer controlled_buffer_10
  assign Ausgang[5] = decoder_1_out4 ? Eingang[1] : 1'bz;  // Controlled_Buffer controlled_buffer_11
  assign Ausgang[4] = decoder_1_out5 ? Eingang[1] : 1'bz;  // Controlled_Buffer controlled_buffer_12
  assign Ausgang[3] = decoder_1_out6 ? Eingang[1] : 1'bz;  // Controlled_Buffer controlled_buffer_13
  assign Ausgang[2] = decoder_1_out7 ? Eingang[1] : 1'bz;  // Controlled_Buffer controlled_buffer_14
  assign Ausgang[1] = decoder_1_out0 ? Eingang[1] : 1'bz;  // Controlled_Buffer controlled_buffer_15
  assign Ausgang[0] = decoder_1_out1 ? Eingang[1] : 1'bz;  // Controlled_Buffer controlled_buffer_16
  assign Ausgang[7] = decoder_1_out3 ? Eingang[2] : 1'bz;  // Controlled_Buffer controlled_buffer_17
  assign Ausgang[6] = decoder_1_out4 ? Eingang[2] : 1'bz;  // Controlled_Buffer controlled_buffer_18
  assign Ausgang[5] = decoder_1_out5 ? Eingang[2] : 1'bz;  // Controlled_Buffer controlled_buffer_19
  assign Ausgang[4] = decoder_1_out6 ? Eingang[2] : 1'bz;  // Controlled_Buffer controlled_buffer_20
  assign Ausgang[3] = decoder_1_out7 ? Eingang[2] : 1'bz;  // Controlled_Buffer controlled_buffer_21
  assign Ausgang[2] = decoder_1_out0 ? Eingang[2] : 1'bz;  // Controlled_Buffer controlled_buffer_22
  assign Ausgang[1] = decoder_1_out1 ? Eingang[2] : 1'bz;  // Controlled_Buffer controlled_buffer_23
  assign Ausgang[0] = decoder_1_out2 ? Eingang[2] : 1'bz;  // Controlled_Buffer controlled_buffer_24
  assign Ausgang[7] = decoder_1_out4 ? Eingang[3] : 1'bz;  // Controlled_Buffer controlled_buffer_25
  assign Ausgang[6] = decoder_1_out5 ? Eingang[3] : 1'bz;  // Controlled_Buffer controlled_buffer_26
  assign Ausgang[5] = decoder_1_out6 ? Eingang[3] : 1'bz;  // Controlled_Buffer controlled_buffer_27
  assign Ausgang[4] = decoder_1_out7 ? Eingang[3] : 1'bz;  // Controlled_Buffer controlled_buffer_28
  assign Ausgang[3] = decoder_1_out0 ? Eingang[3] : 1'bz;  // Controlled_Buffer controlled_buffer_29
  assign Ausgang[2] = decoder_1_out1 ? Eingang[3] : 1'bz;  // Controlled_Buffer controlled_buffer_30
  assign Ausgang[1] = decoder_1_out2 ? Eingang[3] : 1'bz;  // Controlled_Buffer controlled_buffer_31
  assign Ausgang[0] = decoder_1_out3 ? Eingang[3] : 1'bz;  // Controlled_Buffer controlled_buffer_32
  assign Ausgang[7] = decoder_1_out5 ? Eingang[4] : 1'bz;  // Controlled_Buffer controlled_buffer_33
  assign Ausgang[6] = decoder_1_out6 ? Eingang[4] : 1'bz;  // Controlled_Buffer controlled_buffer_34
  assign Ausgang[5] = decoder_1_out7 ? Eingang[4] : 1'bz;  // Controlled_Buffer controlled_buffer_35
  assign Ausgang[4] = decoder_1_out0 ? Eingang[4] : 1'bz;  // Controlled_Buffer controlled_buffer_36
  assign Ausgang[3] = decoder_1_out1 ? Eingang[4] : 1'bz;  // Controlled_Buffer controlled_buffer_37
  assign Ausgang[2] = decoder_1_out2 ? Eingang[4] : 1'bz;  // Controlled_Buffer controlled_buffer_38
  assign Ausgang[1] = decoder_1_out3 ? Eingang[4] : 1'bz;  // Controlled_Buffer controlled_buffer_39
  assign Ausgang[0] = decoder_1_out4 ? Eingang[4] : 1'bz;  // Controlled_Buffer controlled_buffer_40
  assign Ausgang[7] = decoder_1_out6 ? Eingang[5] : 1'bz;  // Controlled_Buffer controlled_buffer_41
  assign Ausgang[6] = decoder_1_out7 ? Eingang[5] : 1'bz;  // Controlled_Buffer controlled_buffer_42
  assign Ausgang[5] = decoder_1_out0 ? Eingang[5] : 1'bz;  // Controlled_Buffer controlled_buffer_43
  assign Ausgang[4] = decoder_1_out1 ? Eingang[5] : 1'bz;  // Controlled_Buffer controlled_buffer_44
  assign Ausgang[3] = decoder_1_out2 ? Eingang[5] : 1'bz;  // Controlled_Buffer controlled_buffer_45
  assign Ausgang[2] = decoder_1_out3 ? Eingang[5] : 1'bz;  // Controlled_Buffer controlled_buffer_46
  assign Ausgang[1] = decoder_1_out4 ? Eingang[5] : 1'bz;  // Controlled_Buffer controlled_buffer_47
  assign Ausgang[0] = decoder_1_out5 ? Eingang[5] : 1'bz;  // Controlled_Buffer controlled_buffer_48
  assign Ausgang[7] = decoder_1_out7 ? Eingang[6] : 1'bz;  // Controlled_Buffer controlled_buffer_49
  assign Ausgang[6] = decoder_1_out0 ? Eingang[6] : 1'bz;  // Controlled_Buffer controlled_buffer_50
  assign Ausgang[5] = decoder_1_out1 ? Eingang[6] : 1'bz;  // Controlled_Buffer controlled_buffer_51
  assign Ausgang[4] = decoder_1_out2 ? Eingang[6] : 1'bz;  // Controlled_Buffer controlled_buffer_52
  assign Ausgang[3] = decoder_1_out3 ? Eingang[6] : 1'bz;  // Controlled_Buffer controlled_buffer_53
  assign Ausgang[2] = decoder_1_out4 ? Eingang[6] : 1'bz;  // Controlled_Buffer controlled_buffer_54
  assign Ausgang[1] = decoder_1_out5 ? Eingang[6] : 1'bz;  // Controlled_Buffer controlled_buffer_55
  assign Ausgang[0] = decoder_1_out6 ? Eingang[6] : 1'bz;  // Controlled_Buffer controlled_buffer_56
  assign Ausgang[7] = decoder_1_out0 ? Eingang[7] : 1'bz;  // Controlled_Buffer controlled_buffer_57
  assign Ausgang[6] = decoder_1_out1 ? Eingang[7] : 1'bz;  // Controlled_Buffer controlled_buffer_58
  assign Ausgang[5] = decoder_1_out2 ? Eingang[7] : 1'bz;  // Controlled_Buffer controlled_buffer_59
  assign Ausgang[4] = decoder_1_out3 ? Eingang[7] : 1'bz;  // Controlled_Buffer controlled_buffer_60
  assign Ausgang[3] = decoder_1_out4 ? Eingang[7] : 1'bz;  // Controlled_Buffer controlled_buffer_61
  assign Ausgang[2] = decoder_1_out5 ? Eingang[7] : 1'bz;  // Controlled_Buffer controlled_buffer_62
  assign Ausgang[1] = decoder_1_out6 ? Eingang[7] : 1'bz;  // Controlled_Buffer controlled_buffer_63
  assign Ausgang[0] = decoder_1_out7 ? Eingang[7] : 1'bz;  // Controlled_Buffer controlled_buffer_64
endmodule

module selectadd (
  input  [7:0] A,
  input  [7:0] B,
  input  En,
  output C1,
  output [7:0] C2
);

  wire not_1_out;
  wire [7:0] multiplexer_1_out;

  not not_1 (not_1_out, En);
  Multiplexer #(.width(8), .enable("false")) multiplexer_1 (
    .in0(B), .in1({8{1'b0}}), .out(multiplexer_1_out), .sel(not_1_out));
  Adder adder_1 (.a(A), .b(multiplexer_1_out), .out({C2[6:0], C1}), .cout(C2[7]));  // open: cin
endmodule

module Register (
  input  Clk,
  input  Reset,
  input  [7:0] Data_Bus_in,
  input  [23:0] Command,
  output [7:0] Data_Bus_out,
  output [9:0] Address_Bus,
  output R_W,
  output Flags,
  output [7:0] Instructions
);

  wire decoder_1_out0, decoder_1_out1, decoder_1_out2, decoder_1_out3, decoder_1_out4, decoder_2_out0,
       decoder_2_out1, decoder_2_out2, decoder_2_out3, not_1_out;
  wire [5:0] alu_1_status;
  wire [7:0] A_2_q, adder_1_out, Addr_H_2_q, Addr_L_2_q, alu_1_r, B_2_q, MBR_2_q, multiplexer_3_out, PC_2_q,
       SP_2_q, subtractor_1_out;

  and and_1 (Flags, Command[10], alu_1_status[5]);
  LED PC (.in(Command[0]));
  LED SP (.in(Command[1]));
  LED MBR (.in(Command[2]));
  LED A (.in(Command[3]));
  LED B (.in(Command[4]));
  LED Reg1 (.in(Command[5]));
  LED reg_out (.in(Command[16]));
  LED Addr_L (.in(Command[6]));
  LED Addr_H (.in(Command[7]));
  LED u_Instructions (.in(Command[8]));
  Register_part PC_2 (.D(multiplexer_3_out), .en(Command[0]), .Q(PC_2_q), .clk(Clk), .clr(Reset));
  Register_part SP_2 (.D(multiplexer_3_out), .en(Command[1]), .Q(SP_2_q), .clk(Clk), .clr(Reset));
  Register_part MBR_2 (.D(multiplexer_3_out), .en(Command[2]), .Q(MBR_2_q), .clk(Clk), .clr(Reset));
  Register_part A_2 (.D(multiplexer_3_out), .en(Command[3]), .Q(A_2_q), .clk(Clk), .clr(Reset));
  Register_part B_2 (.D(multiplexer_3_out), .en(Command[4]), .Q(B_2_q), .clk(Clk), .clr(Reset));
  Register_part Reg1_2 (.D(multiplexer_3_out), .en(Command[5]), .clk(Clk), .clr(Reset));  // open: Q
  Register_part Addr_L_2 (.D(multiplexer_3_out), .en(Command[6]), .Q(Addr_L_2_q), .clk(Clk), .clr(Reset));
  Register_part Addr_H_2 (.D(multiplexer_3_out), .en(Command[7]), .Q(Addr_H_2_q), .clk(Clk), .clr(Reset));
  Register_part Instructions_2 (.D(multiplexer_3_out), .en(Command[8]), .Q(Instructions), .clk(Clk), .clr(Reset));
  Adder adder_1 (.a(PC_2_q), .b(8'h1), .out(adder_1_out));  // open: cin, cout
  Subtractor subtractor_1 (.a(SP_2_q), .b(8'h1), .out(subtractor_1_out));  // open: bin, bout
  ALU alu_1 (.F(Command[20:17]), .A(A_2_q), .B(B_2_q), .R(alu_1_r), .Status(alu_1_status));
  // Probe on Command[20:17]
  Multiplexer #(.select(2), .width(2), .enable("false")) multiplexer_1 (
    .in0(2'b00), .in1(2'b00), .in2(Addr_H_2_q[1:0]), .in3(2'b00), .out(Address_Bus[9:8]), .sel(Command[12:11]));
  // Probe on alu_1_r
  Multiplexer #(.select(2), .width(8), .enable("false")) multiplexer_2 (
    .in0(PC_2_q), .in1(SP_2_q), .in2(Addr_L_2_q), .in3(alu_1_r), .out(Address_Bus[7:0]), .sel(Command[12:11]));
  Multiplexer #(.select(3), .width(8)) multiplexer_3 (
    .in0(adder_1_out), .in1(subtractor_1_out), .in2(MBR_2_q), .in3(alu_1_r), .out(multiplexer_3_out),
    .sel(Command[15:13]), .en(Command[16]));  // open: in4, in5, in6, in7
  // Probe on alu_1_status[5]
  Decoder #(.select(3), .enable("false")) decoder_1 (
    .out0(decoder_1_out0), .out1(decoder_1_out1), .out2(decoder_1_out2), .out3(decoder_1_out3),
    .out4(decoder_1_out4), .sel(Command[15:13]));  // open: out5, out6, out7
  not not_1 (not_1_out, Command[16]);
  LED PC_3 (.in(decoder_1_out0));
  LED SP_3 (.in(decoder_1_out1));
  LED MBR_3 (.in(decoder_1_out2));
  LED ALU_2 (.in(decoder_1_out3));
  LED reg1_3 (.in(decoder_1_out4));
  assign Data_Bus_out = R_W ? multiplexer_3_out : 8'bz;  // Controlled_Buffer controlled_buffer_1
  assign multiplexer_3_out = not_1_out ? Data_Bus_in : 8'bz;  // Controlled_Buffer controlled_buffer_2
  or or_1 (R_W, Command[16], Command[9]);
  Decoder #(.select(2), .enable("false")) decoder_2 (
    .out0(decoder_2_out0), .out1(decoder_2_out1), .out2(decoder_2_out2), .out3(decoder_2_out3),
    .sel(Command[12:11]));
  LED PC_4 (.in(decoder_2_out0));
  LED SP_4 (.in(decoder_2_out1));
  LED Addr_L_3 (.in(decoder_2_out2));
  LED ALU_3 (.in(decoder_2_out3));
endmodule

module CPU (
  input  Reset,
  input  [7:0] Data_Bus_in,
  input  Clk,
  output [7:0] Data_Bus_out,
  output [9:0] Address_Bus,
  output R_W
);

  wire decoder_1_out0, decoder_1_out1, decoder_1_out2, decoder_1_out3, decoder_1_out4, decoder_1_out5,
       decoder_1_out6, decoder_1_out7;
  wire [2:0] counter_1_q, register_2_instructions;
  wire [4:0] register_2_instructions_2;
  wire [8:8] register_2_flags;
  wire [23:0] register_1_q, rom_1_data;

  Counter #(.width(3), .max('h7)) counter_1 (.Q(counter_1_q), .clk(Clk), .clr(Reset));  // open: load, D, count, carry
  Decoder #(.select(3), .enable("false")) decoder_1 (
    .out0(decoder_1_out0), .out1(decoder_1_out1), .out2(decoder_1_out2), .out3(decoder_1_out3),
    .out4(decoder_1_out4), .out5(decoder_1_out5), .out6(decoder_1_out6), .out7(decoder_1_out7),
    .sel(counter_1_q));
  LED _1 (.in(decoder_1_out0));
  LED _2 (.in(decoder_1_out1));
  LED _3 (.in(decoder_1_out2));
  LED _4 (.in(decoder_1_out3));
  LED _5 (.in(decoder_1_out4));
  LED _6 (.in(decoder_1_out5));
  LED _7 (.in(decoder_1_out6));
  LED _8 (.in(decoder_1_out7));
  ROM #(.addrWidth(9), .dataWidth(24)) rom_1 (
    .addr({register_2_flags[8], register_2_instructions_2, counter_1_q}), .data(rom_1_data), .sel(1'b1));
  Register_part #(.width(24)) register_1 (.D(rom_1_data), .Q(register_1_q), .clk(Clk), .clr(Reset));  // open: en
  // Probe on {register_2_instructions, register_2_instructions_2}
  Register register_2 (
    .Clk(Clk), .Reset(Reset), .Command(register_1_q), .Flags(register_2_flags[8]),
    .Instructions({register_2_instructions, register_2_instructions_2}), .Data_Bus_out(Data_Bus_out),
    .Data_Bus_in(Data_Bus_in), .Address_Bus(Address_Bus), .R_W(R_W));

  // Notes on the sheet:
  //   contents of rom_1 (hex, n*v repeats v):
  //   100 10001 2 4*0 10001 100 10001 1 4*0 10001 100 10001 2 4*0 10001 100 10001 8 4*0 10001 100 10001 10
  //   4*0 10001 100 10001 20 4*0 10001 100 10001 40 4*0 10001 100 10001 80 4*0 10001 100
endmodule

module main (
);

  wire Clk_out, cpu_1_r_w, decoder_1_out0, decoder_1_out1, decoder_1_out2, Reset_out, xor_1_out;
  wire [7:0] cpu_1_data_bus_out;
  wire [9:0] cpu_1_address_bus;

  Button Reset (.out(Reset_out));
  Clock Clk (.out(Clk_out));
  CPU cpu_1 (
    .Reset(Reset_out), .Clk(Clk_out), .Data_Bus_out(cpu_1_data_bus_out), .Data_Bus_in(cpu_1_data_bus_out),
    .Address_Bus(cpu_1_address_bus), .R_W(cpu_1_r_w));
  // Probe on cpu_1_address_bus
  // Probe on cpu_1_data_bus_out
  // Probe on cpu_1_r_w
  Decoder #(.select(2), .enable("false")) decoder_1 (
    .out0(decoder_1_out0), .out1(decoder_1_out1), .out2(decoder_1_out2), .sel(cpu_1_address_bus[9:8]));  // open: out3
  xor xor_1 (xor_1_out, cpu_1_r_w, decoder_1_out0);
  TTY tty_1 (.data(cpu_1_data_bus_out[6:0]), .clk(Clk_out), .we(decoder_1_out2), .clr(Reset_out));
  ROM rom_1 (.addr(cpu_1_address_bus[7:0]), .data(cpu_1_data_bus_out), .sel(xor_1_out));
  RAM #(.bus("separate")) ram_1 (
    .addr(cpu_1_address_bus[7:0]), .din(cpu_1_data_bus_out), .data(cpu_1_data_bus_out), .str(cpu_1_r_w),
    .sel(decoder_1_out1), .clk(Clk_out), .ld(decoder_1_out1), .clr(Reset_out));
endmodule
