// Logisim project Würfel.circ as structural Verilog: 1 circuit, main circuit main
module main (
  input  in_1
);

  wire clock_1_out;
  wire [6:0] _1_out, register_1_q;
  wire [7:4] rom_1_data;

  Button _1 (.out(_1_out[4]));
  Button _2 (.out(_1_out[5]));
  Button S (.out(_1_out[6]));
  Register #(.width(7)) register_1 (.D(_1_out), .Q(register_1_q), .clk(clock_1_out));  // open: en, clr
  Clock clock_1 (.out(clock_1_out));
  ROM #(.addrWidth(7)) rom_1 (.addr(register_1_q), .data({rom_1_data, _1_out[3:0]}), .sel(in_1));
  LED #(.active("false")) led_1 (.in(rom_1_data[4]));
  LED #(.active("false")) led_2 (.in(rom_1_data[6]));
  LED #(.active("false")) led_3 (.in(rom_1_data[5]));
  LED #(.active("false")) led_4 (.in(rom_1_data[5]));
  LED #(.active("false")) led_5 (.in(rom_1_data[6]));
  LED #(.active("false")) led_6 (.in(rom_1_data[7]));
  LED #(.active("false")) led_7 (.in(rom_1_data[4]));

  // Notes on the sheet:
  //   contents of rom_1 (hex, n*v repeats v):
  //   16*0 71 e2 63 c4 45 80 10*0 85 70 e1 62 c3 44 26*0 41 e2 83 c4 75 86 67 80
endmodule
