// Logisim project Oszi.circ as structural Verilog: 1 circuit, main circuit main
module main (
  input  [4:0] in_1,
  input  Frequenz,
  input  Form,
  input  in_4,
  input  reset
);

  wire clock_1_out;
  wire [4:0] adder_1_out, counter_1_q, counter_2_q, register_2_q;
  wire [6:0] register_3_q;
  wire [7:0] demultiplexer_1_out0, demultiplexer_1_out1, demultiplexer_1_out2, demultiplexer_1_out3,
       demultiplexer_1_out4, demultiplexer_1_out5, demultiplexer_1_out6, demultiplexer_1_out7,
       demultiplexer_1_out8, demultiplexer_1_out9, demultiplexer_1_out10, demultiplexer_1_out11,
       demultiplexer_1_out12, demultiplexer_1_out13, demultiplexer_1_out14, demultiplexer_1_out15,
       demultiplexer_1_out16, demultiplexer_1_out17, demultiplexer_1_out18, demultiplexer_1_out19,
       demultiplexer_1_out20, demultiplexer_1_out21, demultiplexer_1_out22, demultiplexer_1_out23,
       demultiplexer_1_out24, demultiplexer_1_out25, demultiplexer_1_out26, demultiplexer_1_out27,
       demultiplexer_1_out28, demultiplexer_1_out29, demultiplexer_1_out30, demultiplexer_1_out31,
       register_1_q, rom_1_data;

  Counter #(.width(5), .max('h1f)) counter_1 (
    .Q(counter_1_q), .clk(clock_1_out), .clr(reset));  // open: load, D, count, carry
  Counter #(.width(5), .max('h1f)) counter_2 (
    .Q(counter_2_q), .clk(clock_1_out), .clr(reset));  // open: load, D, count, carry
  Register register_1 (.D(rom_1_data), .Q(register_1_q), .clk(clock_1_out), .clr(reset));  // open: en
  Register #(.width(5)) register_2 (.D(counter_2_q), .Q(register_2_q), .clk(clock_1_out), .clr(reset));  // open: en
  Clock clock_1 (.out(clock_1_out));
  Adder #(.width(5)) adder_1 (.a(in_1), .b(counter_1_q), .out(adder_1_out));  // open: cin, cout
  DotMatrix #(.matrixcols(32), .matrixrows(8), .persist(64)) dotmatrix_1 (
    .col0(demultiplexer_1_out0), .col1(demultiplexer_1_out1), .col2(demultiplexer_1_out2),
    .col3(demultiplexer_1_out3), .col4(demultiplexer_1_out4), .col5(demultiplexer_1_out5),
    .col6(demultiplexer_1_out6), .col7(demultiplexer_1_out7), .col8(demultiplexer_1_out8),
    .col9(demultiplexer_1_out9), .col10(demultiplexer_1_out10), .col11(demultiplexer_1_out11),
    .col12(demultiplexer_1_out12), .col13(demultiplexer_1_out13), .col14(demultiplexer_1_out14),
    .col15(demultiplexer_1_out15), .col16(demultiplexer_1_out16), .col17(demultiplexer_1_out17),
    .col18(demultiplexer_1_out18), .col19(demultiplexer_1_out19), .col20(demultiplexer_1_out20),
    .col21(demultiplexer_1_out21), .col22(demultiplexer_1_out22), .col23(demultiplexer_1_out23),
    .col24(demultiplexer_1_out24), .col25(demultiplexer_1_out25), .col26(demultiplexer_1_out26),
    .col27(demultiplexer_1_out27), .col28(demultiplexer_1_out28), .col29(demultiplexer_1_out29),
    .col30(demultiplexer_1_out30), .col31(demultiplexer_1_out31));
  Register #(.width(7)) register_3 (
    .D({Form, Frequenz, adder_1_out}), .Q(register_3_q), .clk(clock_1_out), .clr(reset));  // open: en
  Demultiplexer #(.select(5), .width(8), .enable("false")) demultiplexer_1 (
    .out0(demultiplexer_1_out0), .out1(demultiplexer_1_out1), .out2(demultiplexer_1_out2),
    .out3(demultiplexer_1_out3), .out4(demultiplexer_1_out4), .out5(demultiplexer_1_out5),
    .out6(demultiplexer_1_out6), .out7(demultiplexer_1_out7), .out8(demultiplexer_1_out8),
    .out9(demultiplexer_1_out9), .out10(demultiplexer_1_out10), .out11(demultiplexer_1_out11),
    .out12(demultiplexer_1_out12), .out13(demultiplexer_1_out13), .out14(demultiplexer_1_out14),
    .out15(demultiplexer_1_out15), .out16(demultiplexer_1_out16), .out17(demultiplexer_1_out17),
    .out18(demultiplexer_1_out18), .out19(demultiplexer_1_out19), .out20(demultiplexer_1_out20),
    .out21(demultiplexer_1_out21), .out22(demultiplexer_1_out22), .out23(demultiplexer_1_out23),
    .out24(demultiplexer_1_out24), .out25(demultiplexer_1_out25), .out26(demultiplexer_1_out26),
    .out27(demultiplexer_1_out27), .out28(demultiplexer_1_out28), .out29(demultiplexer_1_out29),
    .out30(demultiplexer_1_out30), .out31(demultiplexer_1_out31), .in(register_1_q), .sel(register_2_q));
  ROM #(.addrWidth(7)) rom_1 (.addr(register_3_q), .data(rom_1_data), .sel(in_4));
endmodule
